# Fritzing sketch schematic (saved by Fritzing 0.8.7b)
breadboards: 1

parts:
  Part1 = Arduino Nano (Rev3.0)
  M1 = DC Motor
  M2 = DC Motor
  Part2 = InvenSense MPU6050
  S1 = H-Bridge with L298N
  VCC1 = Battery block 9V

nets:
  GND: Part1.GND, Part2.GND, S1.GND, VCC1.-
  N1: Part1.D2, Part2.INT
  N2: Part1.D10, S1.IN1, S1.IN3
  N3: Part1.D11/MOSI, S1.IN2, S1.IN4
  VIN: Part1.VIN, S1.12V, VCC1.+
  5V: Part1.5V, Part2.VCC
  N4: Part1.A5, Part2.SCL
  N5: Part1.A4, Part2.SDA
  N6: M1.pin_1, S1.M2-02
  N7: M1.pin_2, S1.M2-01
  N8: M2.pin_1, S1.M1-02
  N9: M2.pin_2, S1.M1-01
  N10: S1.ENA, S1.ENA-5V
  N11: S1.ENB, S1.ENB-5V

custom parts:
  H-Bridge with L298N: h-bridge
